# Fritzing sketch final assignment THEN (saved by Fritzing 0.9.3b)

parts:
  Part3 = Lilypad Arduino Board
  Part9 = Breakout Board for Electret Microphone
  U6 = Vibration Motor- ROB-08449 [package=vibe-motor-10mm]
  Part12 = Power Cell LiPo Charger/Booster
  U9 = Vibration Motor- ROB-08449 [package=vibe-motor-10mm]
  BAT1 = LIPO-1000mAh [package=lipo-1000]
  Part18 = NeoPixel Stick [part_number=1426]
  Part21 = Breakout Board for Electret Microphone

nets:
  GND: Part3.GND, Part9.GND, U6.-, Part12.GND, U9.-, BAT1.-, Part18.GND, Part21.GND
  VCC: Part3.VCC, Part9.VCC, Part12.VCC, Part12.VBATT, BAT1.+, Part18.+5V, Part21.VCC
  N1: Part3.A0, Part9.AUD
  N2: Part3.A1, Part21.AUD
  N3: Part3.A2, U9.+
  N4: Part3.A4, U6.+
  N5: Part3.D3, Part18.DATAIN

notes:
  anode cathode are reversed in this diagram]
  There are two identical circuits for both sides of the item.

custom parts:
  NeoPixel Stick: Make your own little LED strip arrangement with this stick of NeoPixel LEDs. We crammed 8 of the tiny 5050 (5mm x 5mm) smart RGB LEDs onto a PCB with mounting holes and a chainable design. Use only one microcontroller pin to control as many as you can chain together! Each LED is addressable as the driver chip is inside the LED. Each one has ~18mA constant current drive so the color will be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
